# Fritzing sketch visualization_02_led_button (saved by Fritzing 1.0.4)
breadboards: 1

parts:
  current_limiting_resistor = Resistor [resistance=220 tolerance=±5% power=0.25W package=THT]
  Arduino1 = Arduino Uno (Rev3)
  Button_(OFF) = Pushbutton [package="[THT]"]
  Button_(ON) = Pushbutton [package="[THT]"]
  LED_(3V) = LED - 3mm [color="Red (633nm)" current=0.030A package="3 mm [THT]"]

nets:
  N1: current_limiting_resistor.Pin_0, Arduino1.D6_PWM
  N2: current_limiting_resistor.Pin_1, LED_(3V).anode
  N3: Arduino1.D8, Button_(OFF).Pin_3, Button_(OFF).Pin_4
  N4: Arduino1.D9_PWM, Button_(ON).Pin_3, Button_(ON).Pin_4
  N5: Arduino1.GND, Button_(OFF).Pin_1, Button_(OFF).Pin_2, Button_(ON).Pin_1, Button_(ON).Pin_2, LED_(3V).cathode
