# Fritzing sketch visualization_01_led_blink (saved by Fritzing 1.0.4)
breadboards: 1

parts:
  current_limiting_resistor = Resistor [resistance=220 tolerance=±5% power=0.25W package=THT]
  LED_(3V) = LED - 3mm [color="Red (633nm)" current=30mA package="3 mm [THT]"]
  Arduino1 = Arduino Uno (Rev3)

nets:
  N1: current_limiting_resistor.Pin_0, Arduino1.D13/SCK
  N2: current_limiting_resistor.Pin_1, LED_(3V).anode
  N3: LED_(3V).cathode, Arduino1.GND

notes:
  (5V - 3V) / 220Ω ≈ 14mA
