# Fritzing sketch visualization_03_led_button_rgb (saved by Fritzing 1.0.4)
circuit board: 6.88566cm x 5.36311cm
breadboards: 1

parts:
  current_limiting_resistor_(R) = Resistor [resistance=220 tolerance=±5% power=0.25W package=THT]
  current_limiting_resistor_(B) = Resistor [resistance=220 tolerance=±5% power=0.25W package=THT]
  current_limiting_resistor_(G) = Resistor [resistance=220 tolerance=±5% power=0.25W package=THT]
  RGB_LED_(3V) = RGB LED (com. cathode, rgb) [color="Red (633nm)" current=0.030A package="5 mm [THT]"]
  Arduino1 = Arduino Uno (Rev3)
  Button_(OFF) = Pushbutton [package="[THT]"]
  Button_(ON) = Pushbutton [package="[THT]"]

nets:
  N1: current_limiting_resistor_(R).Pin_0, Arduino1.D6_PWM
  N2: current_limiting_resistor_(R).Pin_1, RGB_LED_(3V).red_anode
  N3: current_limiting_resistor_(B).Pin_0, Arduino1.D3_PWM
  N4: current_limiting_resistor_(B).Pin_1, RGB_LED_(3V).blue_anode
  N5: current_limiting_resistor_(G).Pin_0, Arduino1.D5_PWM
  N6: current_limiting_resistor_(G).Pin_1, RGB_LED_(3V).green_anode
  N7: RGB_LED_(3V).common_cathode, Arduino1.GND, Button_(OFF).Pin_1, Button_(OFF).Pin_2, Button_(ON).Pin_1, Button_(ON).Pin_2
  N8: Arduino1.D8, Button_(OFF).Pin_3, Button_(OFF).Pin_4
  N9: Arduino1.D9_PWM, Button_(ON).Pin_3, Button_(ON).Pin_4
