# Fritzing sketch 01_trash_notifier_e_ink (saved by Fritzing 1.0.4)
breadboards: 1

parts:
  Raspberry_Pi_3B = Raspberry Pi 3 [part_number=RPI-3-V1.2]
  LED_(bring_in) = smd LED [color="Yellow (595nm)" package="1206 [SMD]"]
  LED_(take_out) = smd LED [color="Red (633nm)" package="1206 [SMD]"]
  RGB_LED_(trash_type) = RGB LED (com. cathode, rgb) [color="Red (633nm)" current=0.030A package="5 mm [THT]"]
  Button_(Take_out_/_Bring_in) = Pushbutton [package="[THT]"]
  R1 = Resistor [tolerance=±5% resistance=220 package="0402 [SMD]"]
  R2 = Resistor [tolerance=±5% resistance=220 package="0402 [SMD]"]
  R3 = Resistor [tolerance=±5% resistance=220 package="0402 [SMD]"]
  R4 = Resistor [tolerance=±5% resistance=220 package="0402 [SMD]"]
  R5 = Resistor [tolerance=±5% resistance=10k package="0402 [SMD]"]
  R6 = Resistor [tolerance=±5% resistance=220 package="0402 [SMD]"]
  Waveshare_1_54inch_e-Paper_Module_200x200 = Waveshare 1.54in epaper display

nets:
  N1: Raspberry_Pi_3B.3v3, Waveshare_1_54inch_e-Paper_Module_200x200.Pin_8
  N2: Raspberry_Pi_3B.GND, LED_(bring_in).cathode, LED_(take_out).cathode, RGB_LED_(trash_type).common_cathode, Button_(Take_out_/_Bring_in).Pin_1, Button_(Take_out_/_Bring_in).Pin_2, Waveshare_1_54inch_e-Paper_Module_200x200.Pin_7
  N3: Raspberry_Pi_3B.GIPO17, Waveshare_1_54inch_e-Paper_Module_200x200.Pin_2
  N4: Raspberry_Pi_3B.GIPO10, Waveshare_1_54inch_e-Paper_Module_200x200.Pin_6
  N5: Raspberry_Pi_3B.GIPO11, Waveshare_1_54inch_e-Paper_Module_200x200.Pin_5
  N6: Raspberry_Pi_3B.GIPO5, R6.Pin_1
  N7: Raspberry_Pi_3B.GIPO6, R4.Pin_1
  N8: Raspberry_Pi_3B.GIPO13, R3.Pin_1
  N9: Raspberry_Pi_3B.GIPO19, R2.Pin_1
  N10: Raspberry_Pi_3B.GIPO26, R1.Pin_1
  N11: Raspberry_Pi_3B.GIPO21, Raspberry_Pi_3B.5V, R5.Pin_1
  N12: Raspberry_Pi_3B.GIPO8, Waveshare_1_54inch_e-Paper_Module_200x200.Pin_4
  N13: Raspberry_Pi_3B.GIPO25, Waveshare_1_54inch_e-Paper_Module_200x200.Pin_3
  N14: Raspberry_Pi_3B.GIPO24, Waveshare_1_54inch_e-Paper_Module_200x200.Pin_1
  N15: LED_(bring_in).anode, R2.Pin_0
  N16: LED_(take_out).anode, R1.Pin_0
  N17: RGB_LED_(trash_type).red_anode, R6.Pin_0
  N18: RGB_LED_(trash_type).green_anode, R4.Pin_0
  N19: RGB_LED_(trash_type).blue_anode, R3.Pin_0
  N20: Button_(Take_out_/_Bring_in).Pin_3, Button_(Take_out_/_Bring_in).Pin_4, R5.Pin_0

custom parts:
  Waveshare 1.54in epaper display: This is an E-Ink display module, 1.54inch, 200x200 resolution, with embedded controller, communicating via SPI interface.
