# Fritzing sketch 02_outdoor_weather (saved by Fritzing 1.0.4)
breadboards: 1

parts:
  Raspberry_Pi_Pico_W = Raspberry Pi Pico W
  DHT22 = DHT22 Humidity and Temperature Sensor
  BMP280 = BME280
  microSD_Adapter_(5V) = MicroSD Card Module

nets:
  N1: Raspberry_Pi_Pico_W.pin_1, BMP280.SDA
  N2: Raspberry_Pi_Pico_W.pin_2, BMP280.SCL
  GND: Raspberry_Pi_Pico_W.pin_3, Raspberry_Pi_Pico_W.pin_8, Raspberry_Pi_Pico_W.pin_13, Raspberry_Pi_Pico_W.pin_18, Raspberry_Pi_Pico_W.pin_23, Raspberry_Pi_Pico_W.pin_28, Raspberry_Pi_Pico_W.pin_33, Raspberry_Pi_Pico_W.pin_38, DHT22.GND, BMP280.GND, microSD_Adapter_(5V).GND
  N3: Raspberry_Pi_Pico_W.pin_4, DHT22.DATA
  N4: Raspberry_Pi_Pico_W.pin_6, microSD_Adapter_(5V).MISO
  N5: Raspberry_Pi_Pico_W.pin_7, microSD_Adapter_(5V).CS
  N6: Raspberry_Pi_Pico_W.pin_9, microSD_Adapter_(5V).SCK
  N7: Raspberry_Pi_Pico_W.pin_10, microSD_Adapter_(5V).MOSI
  VDD: Raspberry_Pi_Pico_W.pin_36, DHT22.VDD, BMP280.VIN
  N8: Raspberry_Pi_Pico_W.pin_40, microSD_Adapter_(5V).VCC

custom parts:
  Raspberry Pi Pico W: Raspberry Pi Pico W. Based around the RP2040 microcontroller the Pico W is a low cost microcontroller device bringing Raspberry Pi quality, cost, and easy of use to the microcontroller space. The areas marked KEEPOUT in pcb silkscreen should not have traces running through them to avoid shorts on a soldered in module!
  BME280: Temperature Humidity Barometric presure Sensor
