# Fritzing sketch visualization_simple_led_button_rgb (saved by Fritzing 1.0.4)
circuit board: 6.88566cm x 5.36311cm
breadboards: 1

parts:
  R4 = Resistor [resistance=220 tolerance=±5% power=0.25W package=THT]
  R5 = Resistor [resistance=220 tolerance=±5% power=0.25W package=THT]
  R6 = Resistor [resistance=220 tolerance=±5% power=0.25W package=THT]
  LED = RGB LED (com. cathode, rgb) [color="Red (633nm)" current=0.030A package="5 mm [THT]"]
  Arduino1 = Arduino Uno (Rev3)
  S1 = Pushbutton [package="[THT]"]
  S2 = Pushbutton [package="[THT]"]

nets:
  N1: R4.Pin_0, Arduino1.D6_PWM
  N2: R4.Pin_1, LED.red_anode
  N3: R5.Pin_0, Arduino1.D3_PWM
  N4: R5.Pin_1, LED.blue_anode
  N5: R6.Pin_0, Arduino1.D5_PWM
  N6: R6.Pin_1, LED.green_anode
  N7: LED.common_cathode, Arduino1.GND, S1.Pin_1, S1.Pin_2, S2.Pin_1, S2.Pin_2
  N8: Arduino1.D8, S1.Pin_3, S1.Pin_4
  N9: Arduino1.D9_PWM, S2.Pin_3, S2.Pin_4
